// Logisim project cpu.circ as structural Verilog: 10 circuits, main circuit main
module main (
  input  reset,
  output [31:0] out_2,
  output [31:0] out_3,
  output out_4,
  output [4:0] out_5,
  output [31:0] out_6,
  output out_7,
  output [31:0] out_8,
  output [31:0] out_9
);

  wire ALUSrc, Branch, clk, ExtControl, Jump, MemtoReg, RegDst, Zero;
  wire [2:0] ALUControl;
  wire [4:0] spt_1__11_15, spt_1__16_20, spt_1__21_25;
  wire [15:0] Imm;
  wire [31:0] dm_1_rd, ext_1_signimm, grf_1_rd1, multiplexer_2_out, PC_prime;

  Clock u_clk (.out(clk));
  PC pc_1 (.PC(PC_prime), .PC_prime(out_3), .clk(clk), .clr(reset));
  CU CU (
    .in(out_2), .RegWrite(out_4), .MemWrite(out_7), .ALUControl(ALUControl), .RegDst(RegDst),
    .MemtoReg(MemtoReg), .ALUSrc(ALUSrc), .Branch(Branch), .Jump(Jump), .ExtControl(ExtControl));
  IM im_1 (.PC(out_3), .Instr(out_2));
  NXTAD nxtad_1 (.PC_prime(PC_prime), .PC(out_3), .Zero(Zero), .Branch(Branch), .Jump(Jump), .Instr(out_2), .Imm(Imm));
  SPT spt_1 (.in(out_2), ._0_15(Imm), ._16_20(spt_1__16_20), ._21_25(spt_1__21_25), ._11_15(spt_1__11_15));
  GRF grf_1 (
    .RD2(out_9), .WD3(out_6), .RD1(grf_1_rd1), .WE3(out_4), .rst(reset), .clk(clk), .A1(spt_1__21_25),
    .A3(out_5), .A2(spt_1__16_20));
  EXT ext_1 (._15_0(Imm), .SignImm(ext_1_signimm), .ExtControl(ExtControl));
  Multiplexer #(.width(5), .enable("false")) multiplexer_1 (
    .in0(spt_1__16_20), .in1(spt_1__11_15), .out(out_5), .sel(RegDst));
  Multiplexer #(.width(32), .enable("false")) multiplexer_2 (
    .in0(out_9), .in1(ext_1_signimm), .out(multiplexer_2_out), .sel(ALUSrc));
  ALU alu_1 (.SrcA(grf_1_rd1), .SrcB(multiplexer_2_out), .ALUResult(out_8), .ALUControl(ALUControl), .Zero(Zero));
  DM dm_1 (.A(out_8), .WD(out_9), .RD(dm_1_rd), .clk(clk), .WE(out_7), .clr(reset));
  Multiplexer #(.width(32), .enable("false")) multiplexer_3 (.in0(out_8), .in1(dm_1_rd), .out(out_6), .sel(MemtoReg));

  // Other names for the same wires on the sheet: Instr[31:0] = out_2; MemAddr[31:0] = out_8; MemData[31:0] = out_9;
  //   MemWrite = out_7; PC[31:0] = out_3; RegAddr[4:0] = out_5; RegData[31:0] = out_6; RegWrite = out_4; rst = reset

  // Notes on the sheet:
  //   SrcB
  //   WriteData
  //   Result
endmodule

module PC (
  input  [31:0] PC,
  input  clk,
  input  clr,
  output [31:0] PC_prime
);

  wire [31:0] register_1_q, subtractor_1_out;

  Subtractor #(.width(32)) subtractor_1 (.a(PC), .b(32'h3000), .out(subtractor_1_out));  // open: bin, bout
  Register #(.width(32)) register_1 (.D(subtractor_1_out), .Q(register_1_q), .clk(clk), .clr(clr));  // open: en
  Adder #(.width(32)) adder_1 (.a(register_1_q), .b(32'h3000), .out(PC_prime));  // open: cin, cout
endmodule

module IM (
  input  [31:0] PC,
  output [31:0] Instr
);

  wire [31:0] subtractor_1_out;

  Subtractor #(.width(32)) subtractor_1 (.a(PC), .b(32'h3000), .out(subtractor_1_out));  // open: bin, bout
  ROM #(.addrWidth(12), .dataWidth(32)) rom_1 (.addr(subtractor_1_out[13:2]), .data(Instr));  // open: sel

  // Notes on the sheet:
  //   contents of rom_1 (hex, n*v repeats v):
  //   3400000a 3401000b 34020016 34030028 340407d0 3485000c 0 0 0 a43020 c23820 e14020 1004820 35020
  //   ad400000 ad410004 ad420008 0 0 0 8d4b0000 8d4c0000 8d4d0000 1407022 1c17822 1e28022 3c11ffff
  //   3c124fff 3c130001 3c140223 36b50001 36d60001 2c4b022 12b6fffe
endmodule

module DM (
  input  [31:0] A,
  input  [31:0] WD,
  input  clk,
  input  WE,
  input  clr,
  output [31:0] RD
);

  wire not_1_out;

  RAM #(.addrWidth(12), .dataWidth(32), .bus("separate")) ram_1 (
    .addr(A[13:2]), .din(WD), .data(RD), .str(WE), .sel(1'b1), .clk(clk), .ld(not_1_out), .clr(clr));
  not not_1 (not_1_out, WE);
endmodule

module GRF (
  input  [31:0] WD3,
  input  [4:0] A2,
  input  [4:0] A3,
  input  WE3,
  input  rst,
  input  clk,
  input  [4:0] A1,
  output [31:0] RD2,
  output [31:0] RD1
);

  wire [31:0] i0, i1, i2, i3, i4, i5, i6, i7, i8, i9, i10, i11, i12, i13, i14, i15, i16, i17, i18, i19, i20,
       i21, i22, i23, i24, i25, i26, i27, i28, i29, i30, i31, o0, o1, o2, o3, o4, o5, o6, o7, o8, o9, o10,
       o11, o12, o13, o14, o15, o16, o17, o18, o19, o20, o21, o22, o23, o24, o25, o26, o27, o28, o29, o30,
       o31;

  Register #(.width(32)) _0 (.D({32{1'b0}}), .en(WE3), .Q(o0), .clk(clk), .clr(rst));
  Register #(.width(32)) _4 (.D(i4), .en(WE3), .Q(o4), .clk(clk), .clr(rst));
  Register #(.width(32)) _8 (.D(i8), .en(WE3), .Q(o8), .clk(clk), .clr(rst));
  Register #(.width(32)) _12 (.D(i12), .en(WE3), .Q(o12), .clk(clk), .clr(rst));
  Register #(.width(32)) _16 (.D(i16), .en(WE3), .Q(o16), .clk(clk), .clr(rst));
  Register #(.width(32)) _20 (.D(i20), .en(WE3), .Q(o20), .clk(clk), .clr(rst));
  Register #(.width(32)) _24 (.D(i24), .en(WE3), .Q(o24), .clk(clk), .clr(rst));
  Register #(.width(32)) _28 (.D(i28), .en(WE3), .Q(o28), .clk(clk), .clr(rst));
  Register #(.width(32)) _1 (.D(i1), .en(WE3), .Q(o1), .clk(clk), .clr(rst));
  Register #(.width(32)) _5 (.D(i5), .en(WE3), .Q(o5), .clk(clk), .clr(rst));
  Register #(.width(32)) _9 (.D(i9), .en(WE3), .Q(o9), .clk(clk), .clr(rst));
  Register #(.width(32)) _13 (.D(i13), .en(WE3), .Q(o13), .clk(clk), .clr(rst));
  Register #(.width(32)) _17 (.D(i17), .en(WE3), .Q(o17), .clk(clk), .clr(rst));
  Register #(.width(32)) _21 (.D(i21), .en(WE3), .Q(o21), .clk(clk), .clr(rst));
  Register #(.width(32)) _25 (.D(i25), .en(WE3), .Q(o25), .clk(clk), .clr(rst));
  Register #(.width(32)) _29 (.D(i29), .en(WE3), .Q(o29), .clk(clk), .clr(rst));
  Register #(.width(32)) _2 (.D(i2), .en(WE3), .Q(o2), .clk(clk), .clr(rst));
  Register #(.width(32)) _6 (.D(i6), .en(WE3), .Q(o6), .clk(clk), .clr(rst));
  Register #(.width(32)) _10 (.D(i10), .en(WE3), .Q(o10), .clk(clk), .clr(rst));
  Register #(.width(32)) _14 (.D(i14), .en(WE3), .Q(o14), .clk(clk), .clr(rst));
  Register #(.width(32)) _18 (.D(i18), .en(WE3), .Q(o18), .clk(clk), .clr(rst));
  Register #(.width(32)) _22 (.D(i22), .en(WE3), .Q(o22), .clk(clk), .clr(rst));
  Register #(.width(32)) _26 (.D(i26), .en(WE3), .Q(o26), .clk(clk), .clr(rst));
  Register #(.width(32)) _30 (.D(i30), .en(WE3), .Q(o30), .clk(clk), .clr(rst));
  Register #(.width(32)) _3 (.D(i3), .en(WE3), .Q(o3), .clk(clk), .clr(rst));
  Register #(.width(32)) _7 (.D(i7), .en(WE3), .Q(o7), .clk(clk), .clr(rst));
  Register #(.width(32)) _11 (.D(i11), .en(WE3), .Q(o11), .clk(clk), .clr(rst));
  Register #(.width(32)) _15 (.D(i15), .en(WE3), .Q(o15), .clk(clk), .clr(rst));
  Register #(.width(32)) _19 (.D(i19), .en(WE3), .Q(o19), .clk(clk), .clr(rst));
  Register #(.width(32)) _23 (.D(i23), .en(WE3), .Q(o23), .clk(clk), .clr(rst));
  Register #(.width(32)) _27 (.D(i27), .en(WE3), .Q(o27), .clk(clk), .clr(rst));
  Register #(.width(32)) _31 (.D(i31), .en(WE3), .Q(o31), .clk(clk), .clr(rst));
  Multiplexer #(.select(5), .width(32), .enable("false")) multiplexer_1 (
    .in0(o0), .in1(o1), .in2(o2), .in3(o3), .in4(o4), .in5(o5), .in6(o6), .in7(o7), .in8(o8), .in9(o9),
    .in10(o10), .in11(o11), .in12(o12), .in13(o13), .in14(o14), .in15(o15), .in16(o16), .in17(o17),
    .in18(o18), .in19(o19), .in20(o20), .in21(o21), .in22(o22), .in23(o23), .in24(o24), .in25(o25),
    .in26(o26), .in27(o27), .in28(o28), .in29(o29), .in30(o30), .in31(o31), .out(RD1), .sel(A1));
  Demultiplexer #(.select(5), .width(32), .tristate("true"), .enable("false")) demultiplexer_1 (
    .out0(i0), .out1(i1), .out2(i2), .out3(i3), .out4(i4), .out5(i5), .out6(i6), .out7(i7), .out8(i8),
    .out9(i9), .out10(i10), .out11(i11), .out12(i12), .out13(i13), .out14(i14), .out15(i15), .out16(i16),
    .out17(i17), .out18(i18), .out19(i19), .out20(i20), .out21(i21), .out22(i22), .out23(i23), .out24(i24),
    .out25(i25), .out26(i26), .out27(i27), .out28(i28), .out29(i29), .out30(i30), .out31(i31), .in(WD3),
    .sel(A3));
  Multiplexer #(.select(5), .width(32), .enable("false")) multiplexer_2 (
    .in0(o0), .in1(o1), .in2(o2), .in3(o3), .in4(o4), .in5(o5), .in6(o6), .in7(o7), .in8(o8), .in9(o9),
    .in10(o10), .in11(o11), .in12(o12), .in13(o13), .in14(o14), .in15(o15), .in16(o16), .in17(o17),
    .in18(o18), .in19(o19), .in20(o20), .in21(o21), .in22(o22), .in23(o23), .in24(o24), .in25(o25),
    .in26(o26), .in27(o27), .in28(o28), .in29(o29), .in30(o30), .in31(o31), .out(RD2), .sel(A2));
endmodule

module ALU (
  input  [2:0] ALUControl,
  input  [31:0] SrcA,
  input  [31:0] SrcB,
  output [31:0] ALUResult,
  output Zero
);

  wire comparator_1_lt, comparator_2_eq, comparator_3_eq;
  wire [31:0] add, \and , lui, \or , slt, sub;

  Adder #(.width(32)) adder_1 (.a(SrcA), .b(SrcB), .out(add));  // open: cin, cout
  Subtractor #(.width(32)) subtractor_1 (.a(SrcA), .b(SrcB), .out(sub));  // open: bin, bout
  Comparator #(.width(32)) comparator_1 (.a(SrcA), .b(SrcB), .lt(comparator_1_lt));  // open: gt, eq
  assign \and  = SrcA & SrcB;  // AND_Gate and_1, 32 bits wide
  assign \or  = SrcA | SrcB;  // OR_Gate or_1, 32 bits wide
  Shifter #(.width(32)) shifter_1 (.in(SrcB), .\dist (5'b10000), .out(lui));
  assign slt = {{31{1'b0}}, comparator_1_lt};  // Bit_Extender bit_extender_1
  Multiplexer #(.select(3), .width(32), .enable("false")) multiplexer_1 (
    .in0(\and ), .in1(\or ), .in2(add), .in3(lui), .in6(sub), .in7(slt), .out(ALUResult), .sel(ALUControl));  // open: in4, in5
  Comparator #(.width(32)) comparator_2 (.a(sub), .b({32{1'b0}}), .eq(comparator_2_eq));  // open: gt, lt
  Comparator #(.width(3)) comparator_3 (.a(ALUControl), .b(3'b110), .eq(comparator_3_eq));  // open: gt, lt
  and and_2 (Zero, comparator_2_eq, comparator_3_eq);

  // Notes on the sheet:
  //   000
  //   001
  //   010
  //   011
  //   110
  //   111
endmodule

module SPT (
  input  [31:0] in,
  output [15:0] _0_15,
  output [4:0] _16_20,
  output [4:0] _21_25,
  output [4:0] _11_15
);


  assign _0_15 = in[15:0];
  assign _11_15 = in[15:11];
  assign _16_20 = in[20:16];
  assign _21_25 = in[25:21];
endmodule

module EXT (
  input  [15:0] _15_0,
  input  ExtControl,
  output [31:0] SignImm
);

  wire [31:0] bit_extender_1_out, bit_extender_2_out;

  assign bit_extender_1_out = {{16{_15_0[15]}}, _15_0};  // Bit_Extender bit_extender_1
  assign bit_extender_2_out = {{16{1'b0}}, _15_0};  // Bit_Extender bit_extender_2
  Multiplexer #(.width(32), .enable("false")) multiplexer_1 (
    .in0(bit_extender_1_out), .in1(bit_extender_2_out), .out(SignImm), .sel(ExtControl));
endmodule

module NXTAD (
  input  Branch,
  input  [31:0] Instr,
  input  Jump,
  input  Zero,
  input  [31:0] PC,
  input  [15:0] Imm,
  output [31:0] PC_prime
);

  wire and_1_out;
  wire [31:0] beq, bit_extender_1_out, multiplexer_1_out, PC_4, shifter_1_out;

  assign bit_extender_1_out = {{16{Imm[15]}}, Imm};  // Bit_Extender bit_extender_1
  Adder #(.width(32)) adder_1 (.a(PC), .b(32'h4), .out(PC_4));  // open: cin, cout
  Shifter #(.width(32)) shifter_1 (.in(bit_extender_1_out), .\dist (5'b00010), .out(shifter_1_out));
  Adder #(.width(32)) adder_2 (.a(shifter_1_out), .b(PC_4), .out(beq));  // open: cin, cout
  and and_1 (and_1_out, Branch, Zero);
  Multiplexer #(.width(32), .enable("false")) multiplexer_1 (
    .in0(PC_4), .in1(beq), .out(multiplexer_1_out), .sel(and_1_out));
  Multiplexer #(.width(32), .enable("false")) multiplexer_2 (
    .in0(multiplexer_1_out), .in1({PC_4[31:28], Instr[25:0], 2'b00}), .out(PC_prime), .sel(Jump));
endmodule

module CU (
  input  [31:0] in,
  output RegWrite,
  output MemWrite,
  output [2:0] ALUControl,
  output ALUSrc,
  output MemtoReg,
  output RegDst,
  output Branch,
  output Jump,
  output ExtControl
);

  wire add, addi, \and , beq, comparator_1_eq, comparator_2_eq, comparator_3_eq, comparator_4_eq,
       comparator_5_eq, j, lui, lw, \or , or_1_out, or_2_out, or_3_out, or_4_out, or_5_out, or_6_out, ori,
       pull_resistor_1_node, \R型指令 , slt, sub, sw;

  Comparator #(.width(6), .mode("unsigned")) comparator_1 (
    .a(in[5:0]), .b(6'b100000), .eq(comparator_1_eq));  // open: gt, lt
  Comparator #(.width(6)) comparator_2 (.a(in[5:0]), .b(6'b100010), .eq(comparator_2_eq));  // open: gt, lt
  Comparator #(.width(6)) comparator_3 (.a(in[5:0]), .b(6'b100100), .eq(comparator_3_eq));  // open: gt, lt
  Comparator #(.width(6)) comparator_4 (.a(in[5:0]), .b(6'b100101), .eq(comparator_4_eq));  // open: gt, lt
  Comparator #(.width(6)) comparator_5 (.a(in[5:0]), .b(6'b101010), .eq(comparator_5_eq));  // open: gt, lt
  Comparator #(.width(6)) comparator_6 (.a(in[31:26]), .b(6'b100011), .eq(lw));  // open: gt, lt
  Comparator #(.width(6)) comparator_7 (.a(in[31:26]), .b(6'b101011), .eq(sw));  // open: gt, lt
  Comparator #(.width(6)) comparator_8 (.a(in[31:26]), .b(6'b000100), .eq(beq));  // open: gt, lt
  Comparator #(.width(6)) comparator_9 (.a(in[31:26]), .b({6{1'b0}}), .eq(\R型指令 ));  // open: gt, lt
  Comparator #(.width(6)) comparator_10 (.a(in[31:26]), .b(6'b001000), .eq(addi));  // open: gt, lt
  Comparator #(.width(6)) comparator_11 (.a(in[31:26]), .b(6'b000010), .eq(j));  // open: gt, lt
  Comparator #(.width(6)) comparator_12 (.a(in[31:26]), .b(6'b001101), .eq(ori));  // open: gt, lt
  Comparator #(.width(6)) comparator_13 (.a(in[31:26]), .b(6'b001111), .eq(lui));  // open: gt, lt
  and and_1 (add, comparator_1_eq, \R型指令 );
  and and_2 (sub, comparator_2_eq, \R型指令 );
  and and_3 (\and , comparator_3_eq, \R型指令 );
  and and_4 (\or , comparator_4_eq, \R型指令 );
  and and_5 (slt, comparator_5_eq, \R型指令 );
  or or_1 (or_1_out, add, sub, \and , \or , slt);
  or or_2 (or_2_out, lw, sw);
  or or_3 (or_3_out, sub, beq);
  or or_4 (or_4_out, or_3_out, or_2_out);
  or or_5 (or_5_out, add, sub, \and , \or , slt);
  Pull_Resistor pull_resistor_1 (.node(pull_resistor_1_node));
  or or_6 (or_6_out, add, or_4_out);
  or or_7 (RegWrite, lui, or_1_out, pull_resistor_1_node, addi, lw, ori);
  or or_8 (MemWrite, pull_resistor_1_node, sw);
  or or_9 (ALUControl[0], lui, pull_resistor_1_node, slt, ori, \or );
  or or_10 (ALUControl[1], slt, pull_resistor_1_node, lui, or_6_out);
  or or_11 (ALUControl[2], slt, pull_resistor_1_node, or_3_out);
  or or_12 (ALUSrc, lui, addi, pull_resistor_1_node, or_2_out, ori);
  or or_13 (MemtoReg, pull_resistor_1_node, lw);
  or or_14 (RegDst, pull_resistor_1_node, or_5_out);
  or or_15 (Branch, pull_resistor_1_node, beq);
  or or_16 (Jump, pull_resistor_1_node, j);
  or or_17 (ExtControl, pull_resistor_1_node, ori, lui);

  // Other names for the same wires on the sheet: Funct[5:0] = in[5:0]; Op[5:0] = in[31:26]

  // Notes on the sheet:
  //   lw
  //   sw
  //   beq
  //   addi
  //   j
  //   ori
  //   lui
  //   001
  //   010
  //   000
  //   010
  //   010
  //   110
  //   110
  //   111
endmodule
